// Logisim project study_1.circ as structural Verilog: 4 circuits, main circuit 测试
module \_5输入  (
  input  In1,
  input  In2,
  input  In3,
  input  In4,
  input  In5,
  output Ot1,
  output Ot2,
  output Ot3
);

  wire and_1_out, and_2_out, and_3_out, and_4_out, not_1_out, not_2_out, not_3_out, not_4_out, not_5_out,
       not_6_out, not_7_out;

  not not_1 (not_1_out, In4);
  not not_2 (not_2_out, In2);
  not not_3 (not_3_out, In4);
  not not_4 (not_4_out, In4);
  not not_5 (not_5_out, In5);
  not not_6 (not_6_out, In4);
  not not_7 (not_7_out, In5);
  or or_1 (Ot3, In5, In4);
  and and_1 (and_1_out, In3, not_1_out);
  and and_2 (and_2_out, In1, not_2_out, not_3_out);
  and and_3 (and_3_out, In3, not_4_out, not_5_out);
  and and_4 (and_4_out, In2, not_6_out, not_7_out);
  or or_2 (Ot1, In5, and_1_out, and_2_out);
  or or_3 (Ot2, and_3_out, and_4_out);
endmodule

module \测试  (
);

  wire button_1_out, button_2_out, button_3_out, button_4_out, button_5_out, led_1_u, led_1_v, led_1_x,
       led_1_y, led_1_z, \七段数码管_1_s , \七段数码管_1_u , \七段数码管_1_v , \七段数码管_1_w , \七段数码管_1_x , \七段数码管_1_y ,
       \七段数码管_1_z ;
  wire [2:0] \n5输入_1_ot1 ;

  Button button_1 (.out(button_1_out));
  Button button_2 (.out(button_2_out));
  Button button_3 (.out(button_3_out));
  Button button_4 (.out(button_4_out));
  Button button_5 (.out(button_5_out));
  led led_1 (
    .a(button_1_out), .b(button_2_out), .c(button_3_out), .d(button_4_out), .e(button_5_out), .x(led_1_x),
    .y(led_1_y), .z(led_1_z), .u(led_1_u), .v(led_1_v));
  \_5输入  \u_5输入_1  (
    .In1(button_1_out), .In2(button_2_out), .In3(button_3_out), .In4(button_4_out), .In5(button_5_out),
    .Ot1(\n5输入_1_ot1 [0]), .Ot2(\n5输入_1_ot1 [1]), .Ot3(\n5输入_1_ot1 [2]));
  LED led_2 (.in(led_1_x));
  LED led_3 (.in(led_1_y));
  LED led_4 (.in(led_1_z));
  LED led_5 (.in(led_1_u));
  LED led_6 (.in(led_1_v));
  // Probe on \n5输入_1_ot1 
  Hex_Digit_Display hex_digit_display_1 (.value({1'b0, \n5输入_1_ot1 }), .dp(1'b1));
  \七段数码管  \u_七段数码管_1  (
    .a(1'b0), .b(\n5输入_1_ot1 [2]), .c(\n5输入_1_ot1 [1]), .d(\n5输入_1_ot1 [0]), .x(\七段数码管_1_x ),
    .y(\七段数码管_1_y ), .z(\七段数码管_1_z ), .u(\七段数码管_1_u ), .v(\七段数码管_1_v ), .w(\七段数码管_1_w ), .s(\七段数码管_1_s ));
  _7_Segment_Display u_7_segment_display_1 (
    .g(\七段数码管_1_x ), .f(\七段数码管_1_y ), .a(\七段数码管_1_z ), .b(\七段数码管_1_u ), .e(\七段数码管_1_v ), .d(\七段数码管_1_w ),
    .c(\七段数码管_1_s ), .dp(1'b1));

  // Notes on the sheet:
  //   按键编码值
  //   16进制显示器
  //   7段管显示
endmodule

module led (
  input  a,
  input  b,
  input  c,
  input  d,
  input  e,
  output x,
  output y,
  output z,
  output u,
  output v
);

  or or_1 (x, e, d, c, b, a);
  or or_2 (y, e, d, c, b);
  or or_3 (z, e, d, c);
  or or_4 (u, e, d);

  assign v = e;
endmodule

module \七段数码管  (
  input  a,
  input  b,
  input  c,
  input  d,
  output x,
  output y,
  output z,
  output u,
  output v,
  output w,
  output s
);

  wire and_1_out, and_2_out, and_3_out, and_4_out, and_5_out, and_6_out, and_7_out, and_8_out, and_9_out,
       and_10_out, and_11_out, and_12_out, and_13_out, and_14_out, and_15_out, and_16_out, and_17_out,
       and_18_out, and_19_out, and_20_out, and_21_out, and_22_out, and_23_out, and_24_out, and_25_out,
       and_26_out, not_1_out, not_2_out, not_3_out, not_4_out, not_5_out, not_6_out, not_7_out, not_8_out,
       not_9_out, not_10_out, not_11_out, not_12_out, not_13_out, not_14_out, not_15_out, not_16_out,
       not_17_out, not_18_out, not_19_out, not_20_out, not_21_out, not_22_out, not_23_out, not_24_out,
       not_25_out, not_26_out, not_27_out, not_28_out, not_29_out, not_30_out, not_31_out, not_32_out,
       not_33_out, not_34_out, not_35_out, not_36_out, not_37_out, not_38_out, not_39_out, not_40_out,
       not_41_out, not_42_out, not_43_out, not_44_out, not_45_out, not_46_out, not_47_out, not_48_out,
       not_49_out, not_50_out, not_51_out, not_52_out;

  not not_1 (not_1_out, a);
  not not_2 (not_2_out, b);
  and and_1 (and_1_out, not_1_out, not_2_out, c);
  not not_3 (not_3_out, a);
  and and_2 (and_2_out, not_3_out, b, not_4_out);
  not not_4 (not_4_out, c);
  not not_5 (not_5_out, a);
  and and_3 (and_3_out, not_5_out, b, not_6_out);
  not not_6 (not_6_out, d);
  not not_7 (not_7_out, b);
  and and_4 (and_4_out, a, not_7_out, not_8_out);
  not not_8 (not_8_out, c);
  not not_9 (not_9_out, a);
  not not_10 (not_10_out, c);
  and and_5 (and_5_out, not_9_out, not_10_out, not_11_out);
  not not_11 (not_11_out, d);
  not not_12 (not_12_out, a);
  and and_6 (and_6_out, not_12_out, b, not_13_out);
  not not_13 (not_13_out, c);
  not not_14 (not_14_out, a);
  and and_7 (and_7_out, not_14_out, b, not_15_out);
  not not_15 (not_15_out, d);
  not not_16 (not_16_out, b);
  and and_8 (and_8_out, a, not_16_out, not_17_out);
  not not_17 (not_17_out, c);
  not not_18 (not_18_out, a);
  not not_19 (not_19_out, b);
  and and_9 (and_9_out, not_18_out, not_19_out, not_20_out);
  not not_20 (not_20_out, d);
  not not_21 (not_21_out, a);
  and and_10 (and_10_out, not_21_out, c);
  not not_22 (not_22_out, a);
  and and_11 (and_11_out, not_22_out, b, d);
  and and_12 (and_12_out, a, not_23_out, not_24_out);
  not not_23 (not_23_out, b);
  not not_24 (not_24_out, c);
  not not_25 (not_25_out, a);
  and and_13 (and_13_out, not_25_out, not_26_out);
  not not_26 (not_26_out, b);
  not not_27 (not_27_out, a);
  not not_28 (not_28_out, c);
  and and_14 (and_14_out, not_27_out, not_28_out, not_29_out);
  not not_29 (not_29_out, d);
  not not_30 (not_30_out, b);
  and and_15 (and_15_out, not_30_out, not_31_out);
  not not_31 (not_31_out, c);
  not not_32 (not_32_out, a);
  and and_16 (and_16_out, not_32_out, c, d);
  not not_33 (not_33_out, b);
  not not_34 (not_34_out, c);
  and and_17 (and_17_out, not_33_out, not_34_out, not_35_out);
  not not_35 (not_35_out, d);
  not not_36 (not_36_out, a);
  and and_18 (and_18_out, not_36_out, c, not_37_out);
  not not_37 (not_37_out, d);
  not not_38 (not_38_out, a);
  not not_39 (not_39_out, b);
  not not_40 (not_40_out, d);
  not not_41 (not_41_out, a);
  not not_42 (not_42_out, b);
  not not_43 (not_43_out, a);
  not not_44 (not_44_out, d);
  not not_45 (not_45_out, a);
  not not_46 (not_46_out, c);
  not not_47 (not_47_out, b);
  not not_48 (not_48_out, c);
  not not_49 (not_49_out, b);
  and and_19 (and_19_out, not_49_out, not_50_out);
  not not_50 (not_50_out, c);
  not not_51 (not_51_out, a);
  and and_20 (and_20_out, not_51_out, d);
  not not_52 (not_52_out, a);
  and and_21 (and_21_out, not_52_out, b);
  or or_1 (x, and_1_out, and_2_out, and_3_out, and_4_out);
  or or_2 (y, and_5_out, and_6_out, and_7_out, and_8_out);
  or or_3 (z, and_9_out, and_10_out, and_11_out, and_12_out);
  or or_4 (u, and_13_out, and_14_out, and_15_out, and_16_out);
  or or_5 (v, and_17_out, and_18_out);
  and and_22 (and_22_out, not_38_out, not_39_out, not_40_out);
  and and_23 (and_23_out, not_41_out, not_42_out, c);
  and and_24 (and_24_out, not_43_out, c, not_44_out);
  and and_25 (and_25_out, not_45_out, b, not_46_out, d);
  and and_26 (and_26_out, a, not_47_out, not_48_out);
  or or_6 (s, and_19_out, and_20_out, and_21_out);
  or or_7 (w, and_22_out, and_23_out, and_24_out, and_25_out, and_26_out);
endmodule
