// Logisim project study_4.circ as structural Verilog: 9 circuits, main circuit main
module main (
  input  D0,
  input  D1,
  input  D2,
  input  D3,
  input  D4,
  input  D5,
  input  D6,
  input  D7,
  input  CLK,
  input  CLR,
  output Q0,
  output Q1,
  output Q2,
  output Q3,
  output Q4,
  output Q5,
  output Q6,
  output Q7
);

  wire not_1_out;

  not not_1 (not_1_out, CLR);
  D_Flip_Flop d_ff_1 (.clk(CLK), .D(D0), .Q(Q0), .en(not_1_out));  // open: Qn, preset, reset
  D_Flip_Flop d_ff_2 (.clk(CLK), .D(D4), .Q(Q4), .en(not_1_out));  // open: Qn, preset, reset
  D_Flip_Flop d_ff_3 (.clk(CLK), .D(D1), .Q(Q1), .en(not_1_out));  // open: Qn, preset, reset
  D_Flip_Flop d_ff_4 (.clk(CLK), .D(D5), .Q(Q5), .en(not_1_out));  // open: Qn, preset, reset
  D_Flip_Flop d_ff_5 (.clk(CLK), .D(D2), .Q(Q2), .en(not_1_out));  // open: Qn, preset, reset
  D_Flip_Flop d_ff_6 (.clk(CLK), .D(D6), .Q(Q6), .en(not_1_out));  // open: Qn, preset, reset
  D_Flip_Flop d_ff_7 (.clk(CLK), .D(D3), .Q(Q3), .en(not_1_out));  // open: Qn, preset, reset
  D_Flip_Flop d_ff_8 (.clk(CLK), .D(D7), .Q(Q7), .en(not_1_out));  // open: Qn, preset, reset
endmodule

module _74ls183 (
  input  in_1,
  input  in_2,
  input  in_3,
  output out_4,
  output out_5,
  output out_6,
  output out_7,
  output out_8,
  output out_9,
  output out_10,
  output out_11
);

  wire decoder_1_out0, decoder_1_out1, decoder_1_out2, decoder_1_out3, decoder_1_out4, decoder_1_out5,
       decoder_1_out6, decoder_1_out7;

  Decoder #(.select(3), .enable("false")) decoder_1 (
    .out0(decoder_1_out0), .out1(decoder_1_out1), .out2(decoder_1_out2), .out3(decoder_1_out3),
    .out4(decoder_1_out4), .out5(decoder_1_out5), .out6(decoder_1_out6), .out7(decoder_1_out7),
    .sel({in_3, in_2, in_1}));
  not not_1 (out_4, decoder_1_out0);
  not not_2 (out_5, decoder_1_out1);
  not not_3 (out_6, decoder_1_out2);
  not not_4 (out_7, decoder_1_out3);
  not not_5 (out_8, decoder_1_out4);
  not not_6 (out_9, decoder_1_out5);
  not not_7 (out_10, decoder_1_out6);
  not not_8 (out_11, decoder_1_out7);
  main main_1 ();  // open: D0, D1, D2, D3, D4, D5, D6, D7, CLK, CLR, Q0, Q1, Q2, Q3, Q4, Q5, Q6, Q7
endmodule

module _74LS138 (
);

  _74ls183 u_74ls183_1 ();  // open: in_1, in_2, in_3, out_4, out_5, out_6, out_7, out_8, out_9, out_10, out_11
endmodule

module _74LS273 (
);

  main main_1 ();  // open: D0, D1, D2, D3, D4, D5, D6, D7, CLK, CLR, Q0, Q1, Q2, Q3, Q4, Q5, Q6, Q7
endmodule

module _74LS175 (
  input  in_1,
  input  in_2,
  input  in_3,
  input  in_4,
  input  in_5,
  input  in_6,
  output out_7,
  output out_8,
  output out_9,
  output out_10,
  output out_11,
  output out_12,
  output out_13,
  output out_14
);

  wire not_1_out;

  not not_1 (not_1_out, in_6);
  D_Flip_Flop d_ff_1 (.clk(in_5), .D(in_1), .Q(out_7), .Qn(out_8), .en(not_1_out));  // open: preset, reset
  D_Flip_Flop d_ff_2 (.clk(in_5), .D(in_2), .Q(out_9), .Qn(out_10), .en(not_1_out));  // open: preset, reset
  D_Flip_Flop d_ff_3 (.clk(in_5), .D(in_3), .Q(out_11), .Qn(out_12), .en(not_1_out));  // open: preset, reset
  D_Flip_Flop d_ff_4 (.clk(in_5), .D(in_4), .Q(out_13), .Qn(out_14), .en(not_1_out));  // open: preset, reset
endmodule

module _74LS374 (
  input  in_1,
  input  in_2,
  input  in_3,
  input  in_4,
  input  in_5,
  input  in_6,
  input  in_7,
  input  in_8,
  input  in_9,
  input  in_10,
  output out_11,
  output out_12,
  output out_13,
  output out_14,
  output out_15,
  output out_16,
  output out_17,
  output out_18
);

  wire d_ff_1_qn, d_ff_2_qn, d_ff_3_qn, d_ff_4_qn, d_ff_5_qn, d_ff_6_qn, d_ff_7_qn, d_ff_8_qn, not_1_out;

  not not_1 (not_1_out, in_10);
  D_Flip_Flop d_ff_1 (.clk(in_1), .D(in_2), .Qn(d_ff_1_qn));  // open: Q, preset, en, reset
  assign out_11 = not_1_out ? ~d_ff_1_qn : 1'bz;  // Controlled_Inverter controlled_inverter_1
  D_Flip_Flop d_ff_2 (.clk(in_1), .D(in_3), .Qn(d_ff_2_qn));  // open: Q, preset, en, reset
  assign out_12 = not_1_out ? ~d_ff_2_qn : 1'bz;  // Controlled_Inverter controlled_inverter_2
  D_Flip_Flop d_ff_3 (.clk(in_1), .D(in_4), .Qn(d_ff_3_qn));  // open: Q, preset, en, reset
  assign out_13 = not_1_out ? ~d_ff_3_qn : 1'bz;  // Controlled_Inverter controlled_inverter_3
  D_Flip_Flop d_ff_4 (.clk(in_1), .D(in_5), .Qn(d_ff_4_qn));  // open: Q, preset, en, reset
  assign out_14 = not_1_out ? ~d_ff_4_qn : 1'bz;  // Controlled_Inverter controlled_inverter_4
  D_Flip_Flop d_ff_5 (.clk(in_1), .D(in_6), .Qn(d_ff_5_qn));  // open: Q, preset, en, reset
  D_Flip_Flop d_ff_6 (.clk(in_1), .D(in_7), .Qn(d_ff_6_qn));  // open: Q, preset, en, reset
  D_Flip_Flop d_ff_7 (.clk(in_1), .D(in_8), .Qn(d_ff_7_qn));  // open: Q, preset, en, reset
  D_Flip_Flop d_ff_8 (.clk(in_1), .D(in_9), .Qn(d_ff_8_qn));  // open: Q, preset, en, reset
  assign out_15 = not_1_out ? ~d_ff_5_qn : 1'bz;  // Controlled_Inverter controlled_inverter_5
  assign out_16 = not_1_out ? ~d_ff_6_qn : 1'bz;  // Controlled_Inverter controlled_inverter_6
  assign out_17 = not_1_out ? ~d_ff_7_qn : 1'bz;  // Controlled_Inverter controlled_inverter_7
  assign out_18 = not_1_out ? ~d_ff_8_qn : 1'bz;  // Controlled_Inverter controlled_inverter_8
endmodule

module _28C16 (
  input  [7:0] in_1,
  input  in_2,
  input  in_3,
  input  in_4,
  output [7:0] out_5
);

  wire not_1_out;

  not not_1 (not_1_out, in_3);
  RAM ram_1 (.addr(in_1), .data(out_5), .sel(in_2), .clk(in_4), .ld(not_1_out), .clr(1'b0));
endmodule

module \微程序控制存储电路  (
  input  in_1,
  input  in_2,
  input  in_3,
  input  [5:0] in_4,
  input  in_5,
  input  in_6,
  input  in_7,
  input  in_8,
  input  in_9,
  input  in_10,
  input  [23:0] in_11,
  input  [7:0] in_12,
  input  [7:0] in_13,
  input  [7:0] in_14,
  input  [5:0] in_15,
  input  [5:0] in_16,
  input  [5:0] in_17
);

  wire multiplexer_1_out, not_1_out, not_2_out;

  not not_1 (not_1_out, in_2);
  not not_2 (not_2_out, in_3);
  Multiplexer multiplexer_1 (.in0(not_1_out), .in1(1'b1), .out(multiplexer_1_out), .sel(in_6));  // open: en
  RAM #(.addrWidth(6)) ram_1 (
    .addr(in_15), .data(in_12), .sel(1'b0), .clk(multiplexer_1_out), .ld(not_2_out), .clr(1'b0));
  _74LS374 u_74ls374_1 (
    .in_1(in_2), .in_2(in_2), .in_3(in_2), .in_4(in_4[2]), .in_5(in_4[3]), .in_6(in_4[4]), .in_7(in_4[5]),
    .in_10(in_1), .out_11(in_15[0]), .out_12(in_15[1]), .out_13(in_15[2]), .out_14(in_15[3]),
    .out_15(in_15[4]), .out_16(in_15[5]));  // open: in_8, in_9, out_17, out_18
  \为地址形成电路  \u_为地址形成电路_1  (
    .in_1(in_2), .in_2(in_2), .in_3(in_4[2]), .in_4(in_4[3]), .in_5(in_4[4]), .in_6(in_4[5]), .in_7(in_4[5]),
    .in_8(in_10), .out_16(in_15[0]), .out_17(in_15[1]), .out_18(in_15[2]), .out_19(in_15[3]),
    .out_20(in_15[4]), .out_21(in_15[5]), .in_9(in_17[0]), .in_10(in_17[1]), .in_11(in_17[2]),
    .in_12(in_17[3]), .in_13(in_17[4]), .in_14(in_17[5]), .in_15(in_6));
  RAM #(.addrWidth(6)) ram_2 (
    .addr(in_15), .data(in_13), .sel(1'b0), .clk(multiplexer_1_out), .ld(not_2_out), .clr(1'b0));
  assign in_14 = in_8 ? ~in_11[7:0] : 8'bz;  // Controlled_Inverter controlled_inverter_1
  assign in_12 = in_8 ? ~in_11[15:8] : 8'bz;  // Controlled_Inverter controlled_inverter_2
  assign in_13 = in_8 ? ~in_11[23:16] : 8'bz;  // Controlled_Inverter controlled_inverter_3
  RAM #(.addrWidth(6)) ram_3 (
    .addr(in_15), .data(in_14), .sel(1'b0), .clk(multiplexer_1_out), .ld(not_2_out), .clr(1'b0));

  assign in_4[1:0] = {2{in_2}};
  assign in_5 = in_4[5];
  assign in_16 = in_14[5:0];

  // Other names for the same wires on the sheet: K1 = in_1; K2 = in_3; K3 = in_6; K4 = in_8; nCLR = in_10; T1 = in_2;
  //   uAJ1[5:0] = {in_4[5:2], {2{in_2}}}; T2 = in_4[5]
endmodule

module \为地址形成电路  (
  input  in_1,
  input  in_2,
  input  in_3,
  input  in_4,
  input  in_5,
  input  in_6,
  input  in_7,
  input  in_8,
  input  in_9,
  input  in_10,
  input  in_11,
  input  in_12,
  input  in_13,
  input  in_14,
  input  in_15,
  output out_16,
  output out_17,
  output out_18,
  output out_19,
  output out_20,
  output out_21
);

  wire not_1_out;
  wire [5:0] d_ff_1_q;

  not not_1 (not_1_out, in_8);
  D_Flip_Flop d_ff_1 (.clk(in_7), .D(in_9), .Q(d_ff_1_q[0]), .en(not_1_out));  // open: Qn, preset, reset
  D_Flip_Flop d_ff_2 (.clk(in_7), .D(in_10), .Q(d_ff_1_q[1]), .en(not_1_out));  // open: Qn, preset, reset
  D_Flip_Flop d_ff_3 (.clk(in_7), .D(in_11), .Q(d_ff_1_q[2]), .en(not_1_out));  // open: Qn, preset, reset
  D_Flip_Flop d_ff_4 (.clk(in_7), .D(in_12), .Q(d_ff_1_q[3]), .en(not_1_out));  // open: Qn, preset, reset
  D_Flip_Flop d_ff_5 (.clk(in_7), .D(in_13), .Q(d_ff_1_q[4]), .en(not_1_out));  // open: Qn, preset, reset
  D_Flip_Flop d_ff_6 (.clk(in_7), .D(in_14), .Q(d_ff_1_q[5]), .en(not_1_out));  // open: Qn, preset, reset
  assign {out_21, out_20, out_19, out_18, out_17, out_16} = in_15 ? ~d_ff_1_q : 6'bz;  // Controlled_Inverter controlled_inverter_1
endmodule
